# Fritzing sketch Xbee (saved by Fritzing 0.9.3b)
breadboards: 1

parts:
  U1 = XBEE-1 [package=xbee-1_lock]
  U2 = TMP36 [package=to-92-kit]
  U3 = LIPO-2000mAh [package=lipo-2000]

nets:
  N1: U1.DOUT, U2.VCC, U3.+
  GND: U1.GND, U2.GND, U3.-
  N2: U1.DIO0, U2.VOUT
