# Fritzing sketch board_base_arduino (saved by Fritzing 0.9.3b)
breadboards: 1

parts:
  U1 = XBEE-1 [package=xbee-1]
  S2 = Momentary Switch [package=ksa_sealed_tac_switch]
  S3 = Momentary Switch [package=ksa_sealed_tac_switch]
  Part1 = Arduino Mega ADK (Rev3)
  R1 = Resistor [tolerance=±5% resistance=220 package="0805 [SMD]"]
  R2 = Resistor [tolerance=±5% resistance=1k package="0805 [SMD]"]

nets:
  N1: U1.DOUT, Part1.3V3
  N2: U1.DIN, Part1.D19/RX1
  N3: U1.DIO12, Part1.D18/TX1
  GND: U1.GND, Part1.GND, R1.Pin_1, R2.Pin_1
  N4: S2.2, Part1.D8_PWM, R1.Pin_0
  N5: S2.3, S3.3, Part1.5V
  N6: S3.2, Part1.D7_PWM, R2.Pin_0
