# Fritzing sketch board_gas_sensor (saved by Fritzing 0.9.3b)
breadboards: 1

parts:
  U5 = XBEE-1 [package=xbee-1_lock]
  BAT1 = Battery Holders [package=lipo-1100mAh]
  BAT2 = Battery Holders [package=lipo-1100mAh]
  5V_voltage_regulator = Voltage Regulator [package=to-92]
  Part1 = Gas Sensor Breakout Board
  R1 = Resistor [tolerance=±5% resistance=1k package="0805 [SMD]"]
  3_3V = Voltage Regulator [package=78xxl]

nets:
  N1: U5.DOUT, 3_3V.IN
  GND: U5.GND, BAT1.-, 5V_voltage_regulator.IN, Part1.GND, R1.Pin_0, 3_3V.OUT
  N2: U5.DIO0, Part1.B1, R1.Pin_1
  N3: BAT1.+, BAT2.-
  GND_2: BAT2.+, 5V_voltage_regulator.GND, 3_3V.GND
  N4: 5V_voltage_regulator.OUT, Part1.A1, Part1.H1
