# Fritzing sketch board_temp_sensor (saved by Fritzing 0.9.3b)
breadboards: 1

parts:
  U1 = XBEE-1 [package=xbee-1_lock]
  U2 = LIPO-2000mAh [package=lipo-2000]
  U3 = TMP36 [package=to-92]
  U4 = V_REG_LD1117VXX [package=78xxl]

nets:
  N1: U1.DOUT, U3.VCC, U4.IN
  GND: U1.GND, U2.-, U3.GND, U4.OUT
  N2: U1.DIO0, U3.VOUT
  N3: U2.+, U4.GND
